// Logisim project cpu.circ as structural Verilog: 1 circuit, main circuit cpu
module cpu (
);

  wire DataMem_p4, RegisterFile_p7, undriven;
  wire [1:0] PCcontrol;
  wire [2:0] undriven_3;
  wire [3:0] undriven_2;
  wire [4:0] multiplexer_2_out;
  wire [25:0] ADD;
  wire [31:0] adder_1_out, DataMem_p3, imm32, multiplexer_3_out, nPC, PC, PC4, RegisterFile_p4, res, rsdata,
       rtdata, shifter_1_out;
  wire [31:26] INS;

  Shifter #(.width(32)) shifter_1 (.in(imm32), .\dist (5'b00010), .out(shifter_1_out));
  Register #(.width(32)) u_PC (.D(nPC), .Q(PC));  // open: en, clk, clr
  Adder #(.width(32)) adder_1 (.a(PC4), .b(shifter_1_out), .out(adder_1_out));  // open: cin, cout
  Adder #(.width(32)) adder_2 (.a(PC), .b(32'h4), .out(PC4));  // open: cin, cout
  assign imm32 = {{16{ADD[15]}}, ADD[15:0]};  // Bit_Extender bit_extender_1
  Multiplexer #(.select(2), .width(32)) multiplexer_1 (
    .in0(PC4), .in1(adder_1_out), .in2(res), .in3({PC[31:28], ADD, 2'b00}), .out(nPC), .sel(PCcontrol));
  // mem InstMem: pin names not known; wires that end beside it: PC, {INS, ADD}
  Multiplexer #(.width(5)) multiplexer_2 (.in0(ADD[20:16]), .in1(ADD[15:11]), .out(multiplexer_2_out), .sel(undriven));
  // regfile RegisterFile: pin names not known; wires that end beside it: ADD[25:21], ADD[20:16], multiplexer_2_out, RegisterFile_p4, rsdata, rtdata, RegisterFile_p7
  Multiplexer #(.width(32)) multiplexer_3 (.in0(rtdata), .in1(imm32), .out(multiplexer_3_out), .sel(RegisterFile_p7));
  ALU alu_1 (
    .reg1(rsdata), .reg2(multiplexer_3_out), .shiftAmount(ADD[10:6]), .operation(undriven_2),
    .branchType(undriven_3), .result(res), .PCcontrol(PCcontrol));  // open: zero
  // mem DataMem: pin names not known; wires that end beside it: res, rtdata, DataMem_p3, DataMem_p4
  Multiplexer #(.width(32)) multiplexer_4 (.in0(DataMem_p3), .in1(res), .out(RegisterFile_p4), .sel(DataMem_p4));

  // Other names for the same wires on the sheet: func[5:0] = ADD[5:0]; imm[15:0] = ADD[15:0]; INS[25:0] = ADD;
  //   sa[4:0] = ADD[10:6]; rd[4:0] = ADD[15:11]; rt[4:0] = ADD[20:16]; rs[4:0] = ADD[25:21]; OP[5:0] = INS

  // Notes on the sheet:
  //   PC Control
  //   from ALUControl
endmodule
